# Fritzing sketch Radio Lolin32+MAX98356 (saved by Fritzing 0.9.9b)
breadboards: 1

parts:
  MCU1 = Wemos Lolin32lite
  LCD1 = TFT 1.8 inch 160x128 w microSD
  Componente1 = Adafruit MAX98357A I2S 3W Class D Amplifier [part_number="Adafruit #3006"]
  Componente2 = Adafruit MAX98357A I2S 3W Class D Amplifier [part_number="Adafruit #3006"]
  R1 = Resistor [tolerance=±5% resistance=220k package=THT]
  R2 = Resistor [tolerance=±5% resistance=510k package=THT]
  SPKR1 = Loudspeaker
  SPKR2 = Loudspeaker
  S1 = Pushbutton [package="[THT]"]
  S2 = Pushbutton [package="[THT]"]
  R3 = Resistor [tolerance=±5% resistance=10k package=THT]

nets:
  N1: MCU1.pin_8, Componente1.DIN, Componente2.DIN
  N2: MCU1.pin_9, Componente1.BCLK, Componente2.BCLK
  N3: MCU1.pin_10, Componente1.LRCLK, Componente2.LRCLK
  GND: MCU1.pin_13, LCD1.pin_1, Componente1.GND, Componente1.GAIN, Componente2.GND, Componente2.GAIN, S1.Pin_1, S1.Pin_2, S2.Pin_1, S2.Pin_2
  N4: MCU1.pin_18, LCD1.pin_6
  N5: MCU1.pin_19, S2.Pin_3, S2.Pin_4
  N6: MCU1.pin_20, S1.Pin_3, S1.Pin_4
  N7: MCU1.pin_21, R3.Pin_0
  N8: MCU1.pin_23, LCD1.pin_10
  N9: MCU1.pin_24, LCD1.pin_7
  N10: MCU1.pin_25, LCD1.pin_8
  N11: MCU1.pin_27, LCD1.pin_9
  VIN: MCU1.pin_28, LCD1.pin2, LCD1.pin_15, Componente1.VIN, Componente2.VIN, R1.Pin_1, R2.Pin_1, R3.Pin_1
  N12: Componente1.SD_MODE, R2.Pin_0
  N13: Componente1.VO-, SPKR2.pin1
  N14: Componente1.VO+, SPKR2.pin2
  N15: Componente2.SD_MODE, R1.Pin_0
  N16: Componente2.VO-, SPKR1.pin1
  N17: Componente2.VO+, SPKR1.pin2

notes:
  CS SCL MOSI DC RST
  A0
  RESET      2 (18)
  DC           18 (24)
  MOSI       23 (25)
  SCL          22 (27)
  CS            5 (23)

custom parts:
  Wemos Lolin32lite: Wemos Lolinlite32 wifi and blue tooth board based on the ESP-32 cpu, digital I/Os 19, analog inputs 6, clock 240mhz, Flash 4Mbytes, lipo battery charger (500ma connection broken out on breadboard but not pcb), usb.
  TFT 1.8 inch 160x128 w microSD: This is the kmr-1.8 spi lcd display available on ebay and others. The 1.8" display has 128x160 color pixels.
  Adafruit MAX98357A I2S 3W Class D Amplifier: Listen to this good news - we now have an all in one digital audio amp breakout board that works incredibly well with the Raspberry Pi! If you're looking for an easy and low cost way to get you digital sound files bumpin' then the MAX08357 I2S Amp Breakout is for you. It takes standard I2S digital audio input and, not only decodes it into analog, but also amplifies it directly into a speaker.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
