# Fritzing sketch Radio Lolin32+PCM5102+PAM8403 (saved by Fritzing 0.9.9b)
breadboards: 1

parts:
  MCU1 = Wemos Lolin32lite
  LCD1 = TFT 1.8 inch 160x128 w microSD
  SPKR1 = Loudspeaker
  SPKR2 = Loudspeaker
  M1 = PAM8403 Stereo Amplifier with Volume Control [part_number=HW-012]
  S1 = Pushbutton [package="[THT]"]
  S2 = Pushbutton [package="[THT]"]
  PCM5102A_I2S_Stereo_DAC1 = PCM5102A I2S Stereo DAC
  R1 = Resistor [tolerance=±5% resistance=10k package=THT]

nets:
  N1: MCU1.pin_8, PCM5102A_I2S_Stereo_DAC1.DIN
  N2: MCU1.pin_9, PCM5102A_I2S_Stereo_DAC1.LRCK
  N3: MCU1.pin_10, PCM5102A_I2S_Stereo_DAC1.BCK
  N4: MCU1.pin_13, LCD1.pin_1, M1.POWER-, S1.Pin_1, S1.Pin_2, S2.Pin_1, S2.Pin_2, PCM5102A_I2S_Stereo_DAC1.GND
  N5: MCU1.pin_18, LCD1.pin_6
  N6: MCU1.pin_19, S1.Pin_3, S1.Pin_4
  N7: MCU1.pin_20, MCU1.pin_21, S2.Pin_3, S2.Pin_4
  N8: MCU1.pin_23, LCD1.pin_10
  N9: MCU1.pin_24, LCD1.pin_7
  N10: MCU1.pin_25, LCD1.pin_8
  N11: MCU1.pin_27, LCD1.pin_9
  N12: MCU1.pin_28, LCD1.pin2, LCD1.pin_15, M1.POWER+, PCM5102A_I2S_Stereo_DAC1.VIN, R1.Pin_1
  N13: SPKR1.pin1, M1.LOUT-
  N14: SPKR1.pin2, M1.LOUT+
  N15: SPKR2.pin1, M1.ROUT-
  N16: SPKR2.pin2, M1.ROUT+
  N17: M1.INPUTL, PCM5102A_I2S_Stereo_DAC1.LROUT
  N18: M1.INPUTG, PCM5102A_I2S_Stereo_DAC1.AGND
  N19: M1.INPUTR, PCM5102A_I2S_Stereo_DAC1.ROUT
  N20: PCM5102A_I2S_Stereo_DAC1.SCK, R1.Pin_0

notes:
  CS SCL MOSI DC RST
  A0
  RESET      2 (18)
  DC           18 (24)
  MOSI       23 (25)
  SCL          22 (27)
  CS            5 (23)
  PCM5102A

custom parts:
  Wemos Lolin32lite: Wemos Lolinlite32 wifi and blue tooth board based on the ESP-32 cpu, digital I/Os 19, analog inputs 6, clock 240mhz, Flash 4Mbytes, lipo battery charger (500ma connection broken out on breadboard but not pcb), usb.
  TFT 1.8 inch 160x128 w microSD: This is the kmr-1.8 spi lcd display available on ebay and others. The 1.8" display has 128x160 color pixels.
  PAM8403 Stereo Amplifier with Volume Control: PAM8403 stereo amplifier module with volume control Descriptive words Links: PAM8403 product datasheet
